# Fritzing sketch emw (saved by Fritzing 0.9.2b)
circuit board: 15.24cm x 10.16cm
breadboards: 1

parts:
  PIN(9-13)11 = FTDI_BASIC [package=ftdi_basic]
  PIN(9-13)12 = FTDI_BASIC [package=ftdi_basic]
  PIN(9-13)13 = FTDI_BASIC [package=ftdi_basic]
  PIN(9-13)14 = FTDI_BASIC [package=ftdi_basic]
  PIN(9-13)15 = FTDI_BASIC [package=ftdi_basic]
  PIN(9-13)16 = FTDI_BASIC [package=ftdi_basic]
  Pad42 = Pad [width=0.7 height=1.45 connect=center]
  Pad43 = Pad [width=0.7 height=1.45 connect=center]
  Pad44 = Pad [width=0.7 height=1.45 connect=center]
  Pad45 = Pad [width=0.7 height=1.45 connect=center]
  Pad46 = Pad [width=0.7 height=1.45 connect=center]
  Pad47 = Pad [width=0.7 height=1.45 connect=center]
  Pad48 = Pad [width=0.7 height=1.45 connect=center]
  Pad49 = Pad [width=0.7 height=1.45 connect=center]
  Pad50 = Pad [width=0.7 height=1.45 connect=center]
  Pad51 = Pad [width=0.7 height=1.45 connect=center]
  Pad52 = Pad [width=0.7 height=1.45 connect=center]  # not connected
  Pad53 = Pad [width=0.7 height=1.45 connect=center]  # not connected
  Pad54 = Pad [width=0.7 height=1.45 connect=center]
  Pad55 = Pad [width=0.7 height=1.45 connect=center]
  Pad56 = Pad [width=0.7 height=1.45 connect=center]  # not connected
  Pad57 = Pad [width=0.7 height=1.45 connect=center]
  Pad58 = Pad [width=0.7 height=1.45 connect=center]
  Pad59 = Pad [width=0.7 height=1.45 connect=center]
  Pad60 = Pad [width=0.7 height=1.45 connect=center]
  Pad61 = Pad [width=0.7 height=1.45 connect=center]
  Pad62 = Pad [width=0.7 height=1.45 connect=center]
  Pad63 = Pad [width=0.7 height=1.45 connect=center]
  Pad64 = Pad [width=0.7 height=1.45 connect=center]
  Pad65 = Pad [width=0.7 height=1.45 connect=center]
  Pad66 = Pad [width=0.7 height=1.45 connect=center]
  Pad67 = Pad [width=0.7 height=1.45 connect=center]
  Pad68 = Pad [width=0.7 height=1.45 connect=center]
  Pad69 = Pad [width=0.7 height=1.45 connect=center]
  Pad70 = Pad [width=0.7 height=1.45 connect=center]  # not connected
  Pad71 = Pad [width=0.7 height=1.45 connect=center]
  Pad72 = Pad [width=0.7 height=1.45 connect=center]
  Pad73 = Pad [width=0.7 height=1.45 connect=center]
  Pad74 = Pad [width=0.7 height=1.45 connect=center]
  Pad75 = Pad [width=0.7 height=1.45 connect=center]
  Pad76 = Pad [width=0.7 height=1.45 connect=center]
  Pad77 = Pad [width=0.7 height=1.45 connect=center]
  Pad78 = Pad [width=0.7 height=1.45 connect=center]
  Pad79 = Pad [width=0.7 height=1.45 connect=center]
  Pad80 = Pad [width=0.7 height=1.45 connect=center]
  Pad81 = Pad [width=0.7 height=1.45 connect=center]
  Pad82 = Pad [width=0.7 height=1.45 connect=center]
  Pad112 = Pad [width=0.7 height=1.45 connect=center]
  Pad83 = Pad [width=0.7 height=1.45 connect=center]
  Pad120 = Pad [width=0.7 height=1.45 connect=center]
  Pad109 = Pad [width=0.7 height=1.45 connect=center]
  Pad114 = Pad [width=0.7 height=1.45 connect=center]
  Pad84 = Pad [width=0.7 height=1.45 connect=center]
  Pad89 = Pad [width=0.7 height=1.45 connect=center]
  Pad113 = Pad [width=0.7 height=1.45 connect=center]
  Pad121 = Pad [width=0.7 height=1.45 connect=center]
  Pad108 = Pad [width=0.7 height=1.45 connect=center]
  Pad115 = Pad [width=0.7 height=1.45 connect=center]
  Pad87 = Pad [width=0.7 height=1.45 connect=center]
  PIN(9-13)19 = FTDI_BASIC [package=ftdi_basic]
  Pad90 = Pad [width=0.7 height=1.45 connect=center]
  Pad85 = Pad [width=0.7 height=1.45 connect=center]
  Pad116 = Pad [width=0.7 height=1.45 connect=center]
  PIN(9-13)20 = FTDI_BASIC [package=ftdi_basic]
  Pad91 = Pad [width=0.7 height=1.45 connect=center]
  PIN(9-13)18 = FTDI_BASIC [package=ftdi_basic]
  Pad117 = Pad [width=0.7 height=1.45 connect=center]
  Pad110 = Pad [width=0.7 height=1.45 connect=center]  # not connected
  Pad92 = Pad [width=0.7 height=1.45 connect=center]  # not connected
  Pad93 = Pad [width=0.7 height=1.45 connect=center]  # not connected
  Pad94 = Pad [width=0.7 height=1.45 connect=center]
  Pad111 = Pad [width=0.7 height=1.45 connect=center]
  Pad95 = Pad [width=0.7 height=1.45 connect=center]
  PIN(9-13)21 = FTDI_BASIC [package=ftdi_basic]
  Pad97 = Pad [width=0.7 height=1.45 connect=center]
  Pad104 = Pad [width=0.7 height=1.45 connect=center]
  Pad118 = Pad [width=0.7 height=1.45 connect=center]
  Pad96 = Pad [width=0.7 height=1.45 connect=center]  # not connected
  Pad106 = Pad [width=0.7 height=1.45 connect=center]
  Pad105 = Pad [width=0.7 height=1.45 connect=center]
  Pad119 = Pad [width=0.7 height=1.45 connect=center]
  PIN(9-13)17 = FTDI_BASIC [package=ftdi_basic]
  Pad107 = Pad [width=0.7 height=1.45 connect=center]
  Pad98 = Pad [width=0.7 height=1.45 connect=center]
  Pad99 = Pad [width=0.7 height=1.45 connect=center]
  PIN(9-13)22 = FTDI_BASIC [package=ftdi_basic]
  Pad100 = Pad [width=0.7 height=1.45 connect=center]
  Pad101 = Pad [width=0.7 height=1.45 connect=center]
  Pad86 = Pad [width=0.7 height=1.45 connect=center]
  Pad102 = Pad [width=0.7 height=1.45 connect=center]
  Pad103 = Pad [width=0.7 height=1.45 connect=center]
  Pad88 = Pad [width=0.7 height=1.45 connect=center]

nets:
  N1: PIN(9-13)11.5, Pad45.pad
  N2: PIN(9-13)11.1, Pad75.pad
  N3: PIN(9-13)11.6, Pad43.pad
  N4: PIN(9-13)11.2, Pad49.pad
  N5: PIN(9-13)11.3, Pad66.pad
  N6: PIN(9-13)11.4, Pad61.pad
  N7: PIN(9-13)12.5, Pad68.pad
  N8: PIN(9-13)12.1, Pad80.pad
  N9: PIN(9-13)12.6, Pad58.pad
  N10: PIN(9-13)12.2, Pad47.pad
  N11: PIN(9-13)12.3, Pad62.pad
  N12: PIN(9-13)12.4, Pad76.pad
  N13: PIN(9-13)13.5, Pad48.pad
  N14: PIN(9-13)13.1, Pad42.pad
  N15: PIN(9-13)13.6, Pad55.pad
  N16: PIN(9-13)13.2, Pad50.pad
  N17: PIN(9-13)13.3, Pad63.pad
  N18: PIN(9-13)13.4, Pad78.pad
  N19: PIN(9-13)14.5, Pad59.pad
  N20: PIN(9-13)14.1, Pad60.pad
  N21: PIN(9-13)14.6, Pad67.pad
  N22: PIN(9-13)14.2, Pad71.pad
  N23: PIN(9-13)14.3, Pad64.pad
  N24: PIN(9-13)14.4, Pad79.pad
  N25: PIN(9-13)15.5, Pad54.pad
  N26: PIN(9-13)15.1, Pad81.pad
  N27: PIN(9-13)15.6, Pad74.pad
  N28: PIN(9-13)15.2, Pad69.pad
  N29: PIN(9-13)15.3, Pad46.pad
  N30: PIN(9-13)15.4, Pad57.pad
  N31: PIN(9-13)16.5, Pad51.pad
  N32: PIN(9-13)16.1, Pad73.pad
  N33: PIN(9-13)16.6, Pad72.pad
  N34: PIN(9-13)16.2, Pad44.pad
  N35: PIN(9-13)16.3, Pad77.pad
  N36: PIN(9-13)16.4, Pad65.pad
  N37: Pad82.pad, PIN(9-13)19.1
  N38: Pad112.pad, PIN(9-13)22.6
  N39: Pad83.pad, PIN(9-13)17.6
  N40: Pad120.pad, PIN(9-13)18.1
  N41: Pad109.pad, PIN(9-13)21.2
  N42: Pad114.pad, PIN(9-13)21.6
  N43: Pad84.pad, PIN(9-13)22.2
  N44: Pad89.pad, PIN(9-13)17.2
  N45: Pad113.pad, PIN(9-13)22.1
  N46: Pad121.pad, PIN(9-13)21.1
  N47: Pad108.pad, PIN(9-13)18.5
  N48: Pad115.pad, PIN(9-13)17.1
  N49: Pad87.pad, PIN(9-13)18.2
  N50: PIN(9-13)19.5, Pad88.pad
  N51: PIN(9-13)19.6, Pad95.pad
  N52: PIN(9-13)19.2, Pad90.pad
  N53: PIN(9-13)19.3, Pad103.pad
  N54: PIN(9-13)19.4, Pad118.pad
  N55: Pad85.pad, PIN(9-13)17.5
  N56: Pad116.pad, PIN(9-13)18.4
  N57: PIN(9-13)20.5, Pad99.pad
  N58: PIN(9-13)20.1, Pad100.pad
  N59: PIN(9-13)20.6, Pad107.pad
  N60: PIN(9-13)20.2, Pad111.pad
  N61: PIN(9-13)20.3, Pad104.pad
  N62: PIN(9-13)20.4, Pad119.pad
  N63: Pad91.pad, PIN(9-13)22.5
  N64: PIN(9-13)18.6, Pad98.pad
  N65: PIN(9-13)18.3, Pad102.pad
  N66: Pad117.pad, PIN(9-13)22.3
  N67: Pad94.pad, PIN(9-13)21.5
  N68: PIN(9-13)21.3, Pad86.pad
  N69: PIN(9-13)21.4, Pad97.pad
  N70: Pad106.pad, PIN(9-13)17.3
  N71: Pad105.pad, PIN(9-13)22.4
  N72: PIN(9-13)17.4, Pad101.pad
